# Fritzing sketch arduino_dht22 (saved by Fritzing 0.9.3b)
circuit board: 9cm x 5.9cm
circuit board: 0.26cm x 0.26cm
breadboards: 1

parts:
  U1 = atmega328 [package=dip]
  Part1 = NRF24L01+ Breakout Board
  J1 = Screw terminal - 2 pins [package=THT]
  J2 = double row female pin header, 8 pins [form="♀ (female)"]
  C3 = Ceramic Capacitor [capacitance=22pF package="100 mil [THT, multilayer]"]
  C4 = Electrolytic Capacitor [capacitance=10µF voltage=6.3V package="100 mil [THT, electrolytic]"]
  XTAL1 = Crystal [frequency="16 Mhz" package=THT]
  C2 = Ceramic Capacitor [capacitance=22pF package="100 mil [THT, multilayer]"]
  S1 = Momentary Switch [package=ksa_sealed_tac_switch]
  DHT22 = Humidity and Temperature Sensor RHT03
  J3 = double row female pin header, 8 pins [form="♀ (female)"]
  R2 = Resistor [tolerance=±5% resistance=10k package=THT]
  R1 = Resistor [tolerance=±5% resistance=10k package=THT]
  D1 = Diode [package=diode-1n4001]

nets:
  N1: U1.RESET, S1.3, S1.4, R1.Pin_1
  N2: U1.D4, Part1.IRQ, J2.pin5, J3.pin5
  VCC: U1.VCC, U1.AVCC, U1.AREF, Part1.VCC, J2.pin8, C4.+, DHT22.Vcc, J3.pin8, R2.Pin_1, R1.Pin_0, D1.C
  GND: U1.GND, Part1.GND, J1.pin1, J2.pin1, C3.0, C4.-, C2.0, S1.1, S1.2, DHT22.GND_2, J3.pin1
  N3: U1.XLAT1, C3.1, XTAL1.pin_1
  N4: U1.XLAT2, XTAL1.pin_0, C2.1
  N5: U1.D5_(PWM), DHT22.Data-signal, R2.Pin_0
  N6: U1.D7, Part1.CE, J2.pin2, J3.pin2
  N7: U1.D8, Part1.CS, J2.pin7, J3.pin7
  N8: U1.D11_(PWM), Part1.MOSI, J2.pin6, J3.pin6
  N9: U1.D12, Part1.MISO, J2.pin4, J3.pin4
  N10: U1.D13, Part1.SCK, J2.pin3, J3.pin3
  N11: J1.pin2, D1.A

notes:
  Rev 1.0
  DHT22 - NRF24 - Atmega328
